# Fritzing sketch wiring (saved by Fritzing 0.9.3b)
breadboards: 1

parts:
  부품1 = Arduino Uno (Rev3)
  S1 = Pushbutton [package="[THT]"]
  S2 = Pushbutton [package="[THT]"]
  S3 = Pushbutton [package="[THT]"]
  R2 = Resistor [tolerance=±5% resistance=220 package=THT]
  RE1 = Rotary Encoder [package=THT]
  LED2 = LED - 5mm [color="Red (633nm)" package="5 mm [THT]"]
  LED1 = LED - 5mm [color="Red (633nm)" package="5 mm [THT]"]
  R3 = Resistor [tolerance=±5% resistance=220 package=THT]
  R4 = Resistor [tolerance=±5% resistance=220 package=THT]
  LED3 = LED - 5mm [color="Red (633nm)" package="5 mm [THT]"]

nets:
  N1: 부품1.A0, RE1.EncoderPinC
  N2: 부품1.D8, S2.Pin_3, S2.Pin_4, R3.Pin_0
  N3: 부품1.D9_PWM, S3.Pin_3, S3.Pin_4, R2.Pin_0
  N4: 부품1.GND, 부품1.D5_PWM, 부품1.D6_PWM, R2.Pin_1, RE1.EncoderPinB, LED2.cathode, LED1.cathode, R3.Pin_1, R4.Pin_1, LED3.cathode
  N5: 부품1.D4, LED1.anode
  N6: 부품1.D7, S1.Pin_3, S1.Pin_4, R4.Pin_0
  N7: 부품1.5V, S1.Pin_1, S1.Pin_2, S2.Pin_1, S2.Pin_2, S3.Pin_1, S3.Pin_2, RE1.EncoderPinA

notes:
  Roverbot Arduino TX
  Roverbot Arduino RX
  Center
  Left
  Right
  Speed
